// Digital circuit iki kapılı araba.dig as structural Verilog
module \iki_kapılı_araba  (
  input  A,
  input  B,
  input  C,
  input  D,
  input  E,
  input  F,
  output warning_1,
  output warning_3,
  output warning_2,
  output safe
);

  wire and_1_out, or_1_out;

  or or_1 (or_1_out, C, D);
  and and_1 (and_1_out, E, F);
  or or_2 (warning_1, A, B);
  xor xor_1 (warning_2, B, C);
  or or_3 (warning_3, or_1_out, and_1_out);
  nor nor_1 (safe, warning_1, warning_3, warning_2);
  LED led_1 (.in(warning_1));
  LED led_2 (.in(warning_2));
  LED led_3 (.in(warning_3));
  LED led_4 (.in(safe));
endmodule
